// Digital circuit cpu.dig as structural Verilog
module cpu (
  input  clk,
  input  RESET,
  output IOEN,
  output IOREN,
  output IOWEN,
  output [7:0] IODATA,
  output [14:0] IOADDR,
  output [7:0] HW,
  output [7:0] LW
);

  wire and_1_out, and_2_out, and_3_out, condition_checker_1_skip, nand_1_out, nand_4_out, nand_5_out,
       nand_6_out, nand_7_out, nand_8_out, nand_9_out, nand_10_out, nand_11_out, nand_12_out, nand_13_out,
       nand_14_out, nand_15_out, not_1_out, oprom_1_bssel, oprom_1_fwen, oprom_1_massel, oprom_1_rwen,
       program_memory_1_p5, program_memory_1_p6, program_memory_1_p7;
  wire [1:0] nand_2_out, oprom_1_pcssel, oprom_1_rssel;
  wire [2:0] program_memory_1_p3, program_memory_1_p4;
  wire [3:0] program_memory_1_p2;
  wire [4:0] _8bit_alu_1_flags;
  wire [7:0] _2x8bit_mux_1_out, _2x16bit_mux_1_p2_2, _4x8bit_mux_1_out, _8bit_alu_1_result,
       program_memory_1_p8;
  wire [7:5] _8bit_alu_1_flags_2;
  wire [15:0] _2x16bit_mux_1_p2, _4x16bit_mux_1_out, _16bit_incrementer_1_out, program_memory_1_p1,
       program_memory_1_p9;

  nand nand_1 (nand_1_out, clk, clk);
  // program_memory program_memory_1: pin names not known; wires that end beside it: program_memory_1_p1, program_memory_1_p2, program_memory_1_p3, program_memory_1_p4, program_memory_1_p5, program_memory_1_p6, program_memory_1_p7, program_memory_1_p8, program_memory_1_p9
  program_counter program_counter_1 (.CLK(clk), .W(_4x16bit_mux_1_out), .R(program_memory_1_p1));
  _4x16bit_mux _4x16bit_mux_1 (
    .SEL(nand_2_out), .IN0({16{1'b0}}), .IN1(_16bit_incrementer_1_out), .IN2(_2x16bit_mux_1_p2),
    .IN3(program_memory_1_p9), .OUT(_4x16bit_mux_1_out));
  condition_checker condition_checker_1 (
    .FLAGS(_8bit_alu_1_flags), .COND(program_memory_1_p3), .SKIP(condition_checker_1_skip));
  oprom oprom_1 (
    .OPCODE(program_memory_1_p2), .SKIP(condition_checker_1_skip), .RWEN(oprom_1_rwen), .FWEN(oprom_1_fwen),
    .MREN(IOREN), .MWEN(IOWEN), .BSSEL(oprom_1_bssel), .MASSEL(oprom_1_massel), .RSSEL(oprom_1_rssel),
    .PCSSEL(oprom_1_pcssel));  // open: HALT
  _16bit_incrementer _16bit_incrementer_1 (.IN(program_memory_1_p1), .OUT(_16bit_incrementer_1_out));
  _4x8bit_mux _4x8bit_mux_1 (
    .SEL(oprom_1_rssel), .IN0(program_memory_1_p8), .IN1(IODATA), .IN2(_8bit_alu_1_result),
    .IN3(_2x16bit_mux_1_p2[7:0]), .OUT(_4x8bit_mux_1_out));
  // _2x16bit_mux _2x16bit_mux_1: pin names not known; wires that end beside it: oprom_1_massel, {_2x16bit_mux_1_p2_2, _2x16bit_mux_1_p2[7:0]}, program_memory_1_p9, {IOEN, IOADDR}
  nand nand_2 (nand_2_out[1], nand_4_out, nand_4_out);
  nand nand_3 (nand_2_out[0], nand_5_out, nand_5_out);
  nand nand_4 (nand_4_out, RESET, oprom_1_pcssel[1]);
  nand nand_5 (nand_5_out, RESET, oprom_1_pcssel[0]);
  // register_file register_file_1: pin names not known; wires that end beside it: nand_1_out, oprom_1_rwen, _4x8bit_mux_1_out, program_memory_1_p6, program_memory_1_p5, program_memory_1_p7, _2x16bit_mux_1_p2[7:0], _2x16bit_mux_1_p2[15:8], _2x16bit_mux_1_p2_2
  nand nand_6 (nand_6_out, IOEN, IOEN);
  _2x8bit_mux _2x8bit_mux_1 (
    .SEL(oprom_1_bssel), .B(_2x16bit_mux_1_p2[15:8]), .A(program_memory_1_p8), .OUT(_2x8bit_mux_1_out));
  nand nand_7 (nand_7_out, IOWEN, nand_6_out);
  nand nand_8 (nand_8_out, IOREN, nand_6_out);
  assign IODATA = nand_15_out ? _2x16bit_mux_1_p2[15:8] : 8'bz;  // Driver driver_1
  _8bit_alu _8bit_alu_1 (
    .A(_2x16bit_mux_1_p2[7:0]), .B(_2x8bit_mux_1_out), .OP(program_memory_1_p4), .CLK(nand_1_out),
    .WFLAGEN(oprom_1_fwen), .FLAGS({_8bit_alu_1_flags_2, _8bit_alu_1_flags}), .RESULT(_8bit_alu_1_result));
  nand nand_9 (nand_9_out, nand_7_out, nand_7_out);
  nand nand_10 (nand_10_out, nand_8_out, nand_8_out);
  nand nand_11 (nand_11_out, nand_9_out, nand_1_out);
  nand nand_12 (nand_12_out, IOREN, IOREN);
  nand nand_13 (nand_13_out, nand_11_out, nand_11_out);
  nand nand_14 (nand_14_out, IOWEN, nand_12_out);
  and and_1 (and_1_out, IOWEN, IOEN);
  nand nand_15 (nand_15_out, nand_14_out, nand_14_out);
  RAMSinglePortSel #(.AddrBits(15), .Bits(8)) ramsingleportsel_1 (
    .A(IOADDR), .CS(1'b1), .WE(nand_13_out), .OE(nand_10_out), .D(IODATA));
  not not_1 (not_1_out, IOADDR[0]);
  and and_2 (and_2_out, and_1_out, IOADDR[0]);
  and and_3 (and_3_out, and_1_out, not_1_out);
  out_register out_register_1 (.DATA(IODATA), .WEN(and_2_out), .OUT(HW));
  out_register out_register_2 (.DATA(IODATA), .WEN(and_3_out), .OUT(LW));

  // Notes on the sheet:
  //   clk: Hz: 100
  //   IO Interface
endmodule
