// Digital circuit oprom.dig as structural Verilog
module oprom (
  input  [3:0] OPCODE,
  input  SKIP,
  output RWEN,
  output FWEN,
  output MREN,
  output MWEN,
  output BSSEL,
  output MASSEL,
  output [1:0] RSSEL,
  output [1:0] PCSSEL
);

  wire nand_1_out, nand_2_out, nand_3_out, nand_4_out, nand_5_out;
  wire [3:0] nand_6_out;

  nand nand_1 (nand_1_out, SKIP, SKIP);
  nand nand_2 (nand_2_out, nand_1_out, OPCODE[0]);
  nand nand_3 (nand_3_out, nand_1_out, OPCODE[1]);
  nand nand_4 (nand_4_out, nand_1_out, OPCODE[2]);
  nand nand_5 (nand_5_out, nand_1_out, OPCODE[3]);
  nand nand_6 (nand_6_out[0], nand_2_out, nand_2_out);
  nand nand_7 (nand_6_out[1], nand_3_out, nand_3_out);
  nand nand_8 (nand_6_out[2], nand_4_out, nand_4_out);
  nand nand_9 (nand_6_out[3], nand_5_out, nand_5_out);
  _16x9bit_mux _16x9bit_mux_1 (
    .SEL(nand_6_out), .IN0(10'h100), .IN1(10'h165), .IN2(10'h145), .IN3(10'h128), .IN4(10'h108),
    .IN5(10'h1c1), .IN6(10'h101), .IN7(10'h200), .IN8(10'h300), .IN9(10'h191), .IN10(10'h181),
    .IN11(10'h193), .IN12(10'h183), .IN13(10'h112), .IN14(10'h102), .IN15(10'h100),
    .OUT({PCSSEL, RSSEL, MASSEL, BSSEL, MWEN, MREN, FWEN, RWEN}));
endmodule
